# Fritzing sketch opabinia (saved by Fritzing 0.9.2b)

parts:
  Raspberry_Pi1 = Raspberry Pi B+
  Part1 = SRF05 Ultrasonic Rangefinder
  Part2 = SRF05 Ultrasonic Rangefinder
  LED2 = LED - 3mm [color="Yellow (595nm)" package="3 mm [THT]"]
  LED1 = LED - 3mm [color="Red (633nm)" package="3 mm [THT]"]
  LED3 = LED - 3mm [color="Green (555nm)" package="3 mm [THT]"]
  LED4 = LED - 3mm [color="Yellow (595nm)" package="3 mm [THT]"]
  LED5 = LED - 3mm [color="Red (633nm)" package="3 mm [THT]"]
  R1 = Resistor [tolerance=±5% resistance=220 package=THT]
  R2 = Resistor [tolerance=±5% resistance=220 package=THT]
  R3 = Resistor [tolerance=±5% resistance=220 package=THT]
  R4 = Resistor [tolerance=±5% resistance=220 package=THT]
  R5 = Resistor [tolerance=±5% resistance=220 package=THT]
  R6 = Resistor [tolerance=±5% resistance=330 package=THT]
  R7 = Resistor [tolerance=±5% resistance=330 package=THT]
  R8 = Resistor [tolerance=±5% resistance=470 package=THT]
  R9 = Resistor [tolerance=±5% resistance=470 package=THT]

nets:
  N1: Raspberry_Pi1.GPIO19, R3.Pin_0
  N2: Raspberry_Pi1.GPIO26, R4.Pin_0
  N3: Raspberry_Pi1.GPIO21, R2.Pin_0
  N4: Raspberry_Pi1.GPIO20, R1.Pin_0
  N5: Raspberry_Pi1.GPIO12, Part2.Trig
  N6: Raspberry_Pi1.GPIO25, R9.Pin_0
  N7: Raspberry_Pi1.GPIO24, R8.Pin_0
  N8: Raspberry_Pi1.GPIO18, Part1.Trig
  N9: Raspberry_Pi1.GND, R9.Pin_1
  N10: Part1.Echo, R6.Pin_1
  N11: Part2.Echo, R7.Pin_1
  N12: LED2.anode, R1.Pin_1
  N13: LED1.anode, R5.Pin_1
  N14: LED3.anode, R2.Pin_1
  N15: LED4.anode, R3.Pin_1
  N16: LED5.anode, R4.Pin_1
